// Logisim project circuit1a.circ as structural Verilog: 1 circuit, main circuit main
module main (
  input  A,
  input  B,
  input  C,
  output out
);

  wire and_1_out, and_2_out, and_3_out, and_4_out, and_5_out, and_6_out, and_7_out, and_8_out, and_9_out,
       and_10_out, and_11_out, and_12_out, not_1_out, not_2_out, not_3_out;

  not not_1 (not_1_out, A);
  not not_2 (not_2_out, B);
  not not_3 (not_3_out, C);
  and and_1 (and_1_out, not_1_out, not_2_out, not_3_out);
  and and_2 (and_2_out, not_1_out, not_2_out);
  and and_3 (and_3_out, and_2_out, C);
  and and_4 (and_4_out, not_1_out, not_3_out);
  and and_5 (and_5_out, and_4_out, B);
  and and_6 (and_6_out, B, C);
  and and_7 (and_7_out, A, B);
  and and_8 (and_8_out, not_1_out, and_6_out);
  and and_9 (and_9_out, not_3_out, and_7_out);
  and and_10 (and_10_out, A, B, C);
  and and_11 (and_11_out, A, C);
  and and_12 (and_12_out, and_11_out, not_2_out);
  or or_1 (out, and_1_out, and_3_out, and_5_out, and_12_out, and_8_out, and_9_out, and_10_out);
endmodule
