// Logisim project fsmnew.circ as structural Verilog: 1 circuit, main circuit main
module main (
  input  in1,
  input  in2,
  output out
);

  wire and_1_out, and_2_out, and_3_out, and_4_out, and_5_out, and_6_out, and_7_out, and_8_out, and_9_out,
       and_10_out, and_11_out, and_12_out, and_13_out, and_14_out, and_15_out, and_16_out, and_17_out,
       and_18_out, and_19_out, and_20_out, and_21_out, and_22_out, and_23_out, and_24_out, clock_1_out, d0,
       d1, d2, notd0, notd1, notd2, notin1, notin2, or_1_out, or_2_out, or_3_out;

  not not_1 (notin1, in1);
  not not_2 (notin2, in2);
  and and_1 (and_1_out, notd2, notd1, notd0, notin1, in2);
  and and_2 (and_2_out, notd2, notd1, notd0, in1, notin2);
  and and_3 (and_3_out, notd2, notd1, d0, in1, notin2);
  and and_4 (and_4_out, notd2, notd1, d0, notin1, in2);
  and and_5 (and_5_out, notd2, d1, notd0, notin1, in2);
  and and_6 (and_6_out, notd2, d1, notd0, notin1, notin2);
  and and_7 (and_7_out, notd2, d1, notd0, in1, in2);
  and and_8 (and_8_out, notd2, d1, d0, notin1, notin2);
  and and_9 (and_9_out, notd2, d1, d0, in1, in2);
  and and_10 (and_10_out, notd2, d1, notd0, in1, notin2);
  and and_11 (and_11_out, notd2, d1, d0, in1, notin2);
  and and_12 (and_12_out, notd2, d1, d0, notin1, in2);
  and and_13 (and_13_out, d2, notd1, notd0, notin1, in2);
  and and_14 (and_14_out, d2, notd1, notd0, in1, notin2);
  or or_1 (or_1_out, and_6_out, and_7_out, and_8_out, and_9_out);
  or or_2 (or_2_out, and_1_out, and_10_out, and_2_out, and_11_out, and_3_out, and_12_out, and_4_out, and_13_out, and_5_out, and_14_out);
  D_Flip_Flop q2 (.D(or_1_out), .clk(clock_1_out), .Q(d2), .Qn(notd2));  // open: preset, reset
  Clock clock_1 (.out(clock_1_out));
  D_Flip_Flop q1 (.D(or_2_out), .clk(clock_1_out), .Q(d1), .Qn(notd1));  // open: preset, reset
  and and_15 (and_15_out, notd2, d1, d0, notin1, notin2);
  and and_16 (and_16_out, notd2, d1, d0, in1, in2);
  and and_17 (and_17_out, d2, notd1, notd0);
  and and_18 (and_18_out, notd2, notd1, notd0, notin1, notin2);
  and and_19 (and_19_out, notd2, notd1, notd0, in1, in2);
  and and_20 (and_20_out, notd2, notd1, d0);
  and and_21 (and_21_out, notd2, d1, notd0, in1, in2);
  and and_22 (and_22_out, notd2, d1, notd0, notin1, notin2);
  or or_3 (or_3_out, and_15_out, and_16_out, and_17_out, and_18_out, and_19_out, and_20_out, and_21_out, and_22_out);
  D_Flip_Flop q0 (.D(or_3_out), .clk(clock_1_out), .Q(d0), .Qn(notd0));  // open: preset, reset
  and and_23 (and_23_out, notd2, d1, d0);
  and and_24 (and_24_out, d2, notd1, notd0);
  or or_4 (out, and_23_out, and_24_out);
endmodule
