// Logisim project wrongfsm.circ as structural Verilog: 1 circuit, main circuit main
module main (
  input  in1,
  input  in2,
  output out
);

  wire and_1_out, and_2_out, and_3_out, and_4_out, and_5_out, and_6_out, and_7_out, and_8_out, and_9_out,
       and_10_out, and_11_out, and_12_out, and_13_out, and_14_out, and_15_out, and_16_out, and_17_out,
       and_18_out, clock_1_out, d0, d1, not_1_out, not_2_out, not_3_out, not_4_out, not_5_out, not_6_out,
       not_7_out, not_8_out, not_9_out, not_10_out, not_11_out, not_12_out, not_13_out, notd0, notd1, Q0_out,
       Q1_out;

  and and_1 (and_1_out, notd1, d0);
  and and_2 (and_2_out, d1, d0);
  not not_1 (not_1_out, in1);
  not not_2 (not_2_out, in2);
  not not_3 (not_3_out, in2);
  not not_4 (not_4_out, in1);
  not not_5 (not_5_out, in2);
  not not_6 (not_6_out, in2);
  not not_7 (not_7_out, in1);
  not not_8 (not_8_out, in1);
  not not_9 (not_9_out, in2);
  not not_10 (not_10_out, in1);
  not not_11 (not_11_out, in2);
  not not_12 (not_12_out, in2);
  not not_13 (not_13_out, in1);
  and and_3 (and_3_out, notd1, d0, not_1_out, not_2_out);
  and and_4 (and_4_out, notd1, d0, not_1_out, in2);
  and and_5 (and_5_out, notd1, d0, in1, not_3_out);
  and and_6 (and_6_out, notd1, d0, in1, in2);
  and and_7 (and_7_out, d1, notd0, not_1_out, not_2_out);
  and and_8 (and_8_out, d1, notd0, in1, in2);
  and and_9 (and_9_out, d1, notd0, not_4_out, in2);
  and and_10 (and_10_out, d1, notd0, not_5_out, in1);
  or or_1 (out, and_1_out, and_2_out);
  and and_11 (and_11_out, notd1, notd0, not_6_out, not_7_out);
  and and_12 (and_12_out, notd1, notd0, in2, in1);
  and and_13 (and_13_out, notd1, d0, not_8_out, in2);
  and and_14 (and_14_out, notd1, d0, in1, not_9_out);
  and and_15 (and_15_out, d1, notd0, not_10_out, in2);
  and and_16 (and_16_out, d1, notd0, not_11_out, in1);
  and and_17 (and_17_out, d1, d0, not_12_out, not_13_out);
  and and_18 (and_18_out, d1, d0, in2, in1);
  Clock clock_1 (.out(clock_1_out));
  or Q0 (Q0_out, and_11_out, and_12_out, and_13_out, and_14_out, and_15_out, and_16_out, and_17_out, and_18_out);
  or Q1 (Q1_out, and_3_out, and_4_out, and_5_out, and_6_out, and_7_out, and_8_out, and_9_out, and_10_out);
  D_Flip_Flop Q1_2 (.D(Q1_out), .clk(clock_1_out), .Q(d1), .Qn(notd1));  // open: preset, reset
  D_Flip_Flop Q0_2 (.D(Q0_out), .clk(clock_1_out), .Q(d0), .Qn(notd0));  // open: preset, reset
endmodule
